# Fritzing sketch BeeCounter (saved by Fritzing 0.9.2b)
circuit board: 18.118cm x 12.4385cm
breadboards: 1

parts:
  LDR = Photocell (LDR) [part_number=12 package=THT]
  R2 = Resistor [tolerance=±5% resistance=220 package=THT]
  LDR1 = Photocell (LDR) [part_number=12 package=THT]
  R3 = Resistor [tolerance=±5% resistance=220 package=THT]
  Composant1 = Analog Digital MUX Breakout
  R4 = Resistor [tolerance=±5% resistance=220 package=THT]
  R5 = Resistor [tolerance=±5% resistance=220 package=THT]
  R6 = Resistor [tolerance=±5% resistance=220 package=THT]
  R7 = Resistor [tolerance=±5% resistance=220 package=THT]
  LDR2 = Photocell (LDR) [part_number=12 package=THT]
  LDR3 = Photocell (LDR) [part_number=12 package=THT]
  LDR4 = Photocell (LDR) [part_number=12 package=THT]
  LDR5 = Photocell (LDR) [part_number=12 package=THT]
  R8 = Resistor [tolerance=±5% resistance=220 package=THT]
  R9 = Resistor [tolerance=±5% resistance=220 package=THT]
  R10 = Resistor [tolerance=±5% resistance=220 package=THT]
  R11 = Resistor [tolerance=±5% resistance=220 package=THT]
  R12 = Resistor [tolerance=±5% resistance=220 package=THT]
  R13 = Resistor [tolerance=±5% resistance=220 package=THT]
  LDR6 = Photocell (LDR) [part_number=12 package=THT]
  LDR7 = Photocell (LDR) [part_number=12 package=THT]
  LDR8 = Photocell (LDR) [part_number=12 package=THT]
  LDR9 = Photocell (LDR) [part_number=12 package=THT]
  LDR10 = Photocell (LDR) [part_number=12 package=THT]
  LDR11 = Photocell (LDR) [part_number=12 package=THT]
  R14 = Resistor [tolerance=±5% resistance=220 package=THT]
  LDR12 = Photocell (LDR) [part_number=12 package=THT]
  R15 = Resistor [tolerance=±5% resistance=220 package=THT]
  LDR13 = Photocell (LDR) [part_number=12 package=THT]
  R16 = Resistor [tolerance=±5% resistance=220 package=THT]
  LDR14 = Photocell (LDR) [part_number=12 package=THT]
  R17 = Resistor [tolerance=±5% resistance=220 package=THT]
  LDR15 = Photocell (LDR) [part_number=12 package=THT]

nets (from the pcb view):
  N1: LDR.pin_0, R2.Pin_1, Composant1.C4
  N2: LDR.pin_1, LDR1.pin_0, Composant1.VCC, LDR2.pin_1, LDR3.pin_0, LDR4.pin_1, LDR5.pin_0, LDR6.pin_0, LDR7.pin_1, LDR8.pin_1, LDR9.pin_1, LDR10.pin_0, LDR11.pin_0, LDR12.pin_0, LDR13.pin_1, LDR14.pin_0, LDR15.pin_1
  N3: R2.Pin_0, R5.Pin_0, R6.Pin_0, R9.Pin_0, R12.Pin_0, R15.Pin_0, R17.Pin_0
  N4: LDR1.pin_1, R3.Pin_0, Composant1.C5
  N5: R3.Pin_1, Composant1.GND, R4.Pin_1, R7.Pin_1, R8.Pin_1, R14.Pin_1, R16.Pin_1
  N6: Composant1.C0, R17.Pin_1, LDR15.pin_0
  N7: Composant1.C1, R16.Pin_0, LDR14.pin_1
  N8: Composant1.C2, R15.Pin_1, LDR13.pin_0
  N9: Composant1.C3, R14.Pin_0, LDR12.pin_1
  N10: Composant1.C6, R5.Pin_1, LDR2.pin_0
  N11: Composant1.C7, R4.Pin_0, LDR3.pin_1
  N12: Composant1.C8, R6.Pin_1, LDR4.pin_0
  N13: Composant1.C9, R7.Pin_0, LDR5.pin_1
  N14: Composant1.C10, R9.Pin_1, LDR9.pin_0
  N15: Composant1.C11, R8.Pin_0, LDR11.pin_1
  N16: Composant1.C12, R11.Pin_1, LDR8.pin_0
  N17: Composant1.C13, R10.Pin_1, R13.Pin_1
  N18: Composant1.C14, R12.Pin_1, LDR7.pin_0
  N19: Composant1.C15, R13.Pin_0, LDR6.pin_1
  N20: R10.Pin_0, LDR10.pin_1
