# Fritzing sketch Jobee (saved by Fritzing 0.9.1b)
breadboards: 1

parts:
  Εξάρτημα2 = Arduino Nano (Rev3.0)
  RTC1 = DS1307 RTC Breakout
  SD_card_module1 = SD Card Module
  DS1 = DS18B20 1-Wire Temperature Sensor [part_number=DS18B20]
  R1 = Resistor [tolerance=±5% resistance=4.7k package=THT]

nets:
  N1: Εξάρτημα2.D2, DS1.DQ, R1.Pin_1
  GND: Εξάρτημα2.GND, SD_card_module1.GND, DS1.GND
  5V: Εξάρτημα2.5V, Εξάρτημα2.A5, RTC1.5V, RTC1.SDA, SD_card_module1.+5, DS1.VDD, R1.Pin_0
  N2: Εξάρτημα2.A4, RTC1.SCL

custom parts:
  DS1307 RTC Breakout: DS1307 Real-time Clock Breakout Board with Battery
  SD Card Module: SD Card Module Slot Socket Reader For Arduino ARM MCU
